// Logisim project final.circ as structural Verilog: 12 circuits, main circuit main
module main (
);

  Round round_1 ();  // open: Rst, RoundNum, MSBData, LSBData, MSBKey, LSBKey, MSBDataOut, LSBDataOut, MSBKeyOut, LSBKeyOut
  Round round_2 ();  // open: Rst, RoundNum, MSBData, LSBData, MSBKey, LSBKey, MSBDataOut, LSBDataOut, MSBKeyOut, LSBKeyOut
endmodule

module SubBytes (
  input  [63:0] MSBI,
  input  [63:0] LSBI,
  output [63:0] MSBO,
  output [63:0] LSBO
);

  SBox sbox_1 (.in_1(MSBI[7:0]), .out_2(MSBO[7:0]));
  SBox sbox_2 (.in_1(MSBI[15:8]), .out_2(MSBO[15:8]));
  SBox sbox_3 (.in_1(MSBI[23:16]), .out_2(MSBO[23:16]));
  SBox sbox_4 (.in_1(MSBI[31:24]), .out_2(MSBO[31:24]));
  SBox sbox_5 (.in_1(MSBI[39:32]), .out_2(MSBO[39:32]));
  SBox sbox_6 (.in_1(MSBI[47:40]), .out_2(MSBO[47:40]));
  SBox sbox_7 (.in_1(MSBI[55:48]), .out_2(MSBO[55:48]));
  SBox sbox_8 (.in_1(MSBI[63:56]), .out_2(MSBO[63:56]));
  SBox sbox_9 (.in_1(LSBI[7:0]), .out_2(LSBO[7:0]));
  SBox sbox_10 (.in_1(LSBI[15:8]), .out_2(LSBO[15:8]));
  SBox sbox_11 (.in_1(LSBI[23:16]), .out_2(LSBO[23:16]));
  SBox sbox_12 (.in_1(LSBI[31:24]), .out_2(LSBO[31:24]));
  SBox sbox_13 (.in_1(LSBI[39:32]), .out_2(LSBO[39:32]));
  SBox sbox_14 (.in_1(LSBI[47:40]), .out_2(LSBO[47:40]));
  SBox sbox_15 (.in_1(LSBI[55:48]), .out_2(LSBO[55:48]));
  SBox sbox_16 (.in_1(LSBI[63:56]), .out_2(LSBO[63:56]));
endmodule

module SBox (
  input  [7:0] in_1,
  output [7:0] out_2
);

  wire [7:0] multiplexer_1_out, multiplexer_2_out, multiplexer_3_out, multiplexer_4_out, multiplexer_5_out,
       multiplexer_6_out, multiplexer_7_out, multiplexer_8_out, multiplexer_9_out, multiplexer_10_out,
       multiplexer_11_out, multiplexer_12_out, multiplexer_13_out, multiplexer_14_out, multiplexer_15_out,
       multiplexer_16_out;

  Multiplexer #(.select(4), .width(8)) multiplexer_1 (
    .in0(8'h63), .in1(8'h7c), .in2(8'h77), .in3(8'h7b), .in4(8'hf2), .in5(8'h6b), .in6(8'h6f), .in7(8'hc5),
    .in8(8'h30), .in9(8'h1), .in10(8'h67), .in11(8'h2b), .in12(8'hfe), .in13(8'hd7), .in14(8'hab),
    .in15(8'h76), .out(multiplexer_1_out), .sel(in_1[3:0]));
  Multiplexer #(.select(4), .width(8)) multiplexer_2 (
    .in0(8'hca), .in1(8'h82), .in2(8'hc9), .in3(8'h7d), .in4(8'hfa), .in5(8'h59), .in6(8'h47), .in7(8'hf0),
    .in8(8'had), .in9(8'hd4), .in10(8'ha2), .in11(8'haf), .in12(8'h9c), .in13(8'ha4), .in14(8'h72),
    .in15(8'hc0), .out(multiplexer_2_out), .sel(in_1[3:0]));
  Multiplexer #(.select(4), .width(8)) multiplexer_3 (
    .in0(8'hb7), .in1(8'hfd), .in2(8'h93), .in3(8'h26), .in4(8'h36), .in5(8'h3f), .in6(8'hf7), .in7(8'hcc),
    .in8(8'h34), .in9(8'ha5), .in10(8'he5), .in11(8'hf1), .in12(8'h71), .in13(8'hd8), .in14(8'h31),
    .in15(8'h15), .out(multiplexer_3_out), .sel(in_1[3:0]));
  Multiplexer #(.select(4), .width(8)) multiplexer_4 (
    .in0(8'h4), .in1(8'hc7), .in2(8'h23), .in3(8'hc3), .in4(8'h18), .in5(8'h96), .in6(8'h5), .in7(8'h9a),
    .in8(8'h7), .in9(8'h12), .in10(8'h80), .in11(8'he2), .in12(8'heb), .in13(8'h27), .in14(8'hb2),
    .in15(8'h75), .out(multiplexer_4_out), .sel(in_1[3:0]));
  Multiplexer #(.select(4), .width(8)) multiplexer_5 (
    .in0(8'h9), .in1(8'h83), .in2(8'h2c), .in3(8'h1a), .in4(8'h1b), .in5(8'h6e), .in6(8'h5a), .in7(8'ha0),
    .in8(8'h52), .in9(8'h3b), .in10(8'hd6), .in11(8'hb3), .in12(8'h29), .in13(8'he3), .in14(8'h2f),
    .in15(8'h84), .out(multiplexer_5_out), .sel(in_1[3:0]));
  Multiplexer #(.select(4), .width(8)) multiplexer_6 (
    .in0(8'h53), .in1(8'hd1), .in2({8{1'b0}}), .in3(8'hed), .in4(8'h20), .in5(8'hfc), .in6(8'hb1),
    .in7(8'h5b), .in8(8'h6a), .in9(8'hcb), .in10(8'hbe), .in11(8'h39), .in12(8'h4a), .in13(8'h4c),
    .in14(8'h58), .in15(8'hcf), .out(multiplexer_6_out), .sel(in_1[3:0]));
  Multiplexer #(.select(4), .width(8)) multiplexer_7 (
    .in0(8'hd0), .in1(8'hef), .in2(8'haa), .in3(8'hfb), .in4(8'h43), .in5(8'h4d), .in6(8'h33), .in7(8'h85),
    .in8(8'h45), .in9(8'hf9), .in10(8'h2), .in11(8'h7f), .in12(8'h50), .in13(8'h3c), .in14(8'h9f),
    .in15(8'ha8), .out(multiplexer_7_out), .sel(in_1[3:0]));
  Multiplexer #(.select(4), .width(8)) multiplexer_8 (
    .in0(8'h51), .in1(8'ha3), .in2(8'h40), .in3(8'h8f), .in4(8'h92), .in5(8'h9d), .in6(8'h38), .in7(8'hf5),
    .in8(8'hbc), .in9(8'hb6), .in10(8'hda), .in11(8'h21), .in12(8'h10), .in13({8{1'b1}}), .in14(8'hf3),
    .in15(8'hd2), .out(multiplexer_8_out), .sel(in_1[3:0]));
  Multiplexer #(.select(4), .width(8)) multiplexer_9 (
    .in0(8'hcd), .in1(8'hc), .in2(8'h13), .in3(8'hec), .in4(8'h5f), .in5(8'h97), .in6(8'h44), .in7(8'h17),
    .in8(8'hc4), .in9(8'ha7), .in10(8'h7e), .in11(8'h3d), .in12(8'h64), .in13(8'h5d), .in14(8'h19),
    .in15(8'h73), .out(multiplexer_9_out), .sel(in_1[3:0]));
  Multiplexer #(.select(4), .width(8)) multiplexer_10 (
    .in0(8'h60), .in1(8'h81), .in2(8'h4f), .in3(8'hdc), .in4(8'h22), .in5(8'h2a), .in6(8'h90), .in7(8'h88),
    .in8(8'h46), .in9(8'hee), .in10(8'hb8), .in11(8'h14), .in12(8'hde), .in13(8'h5e), .in14(8'hb),
    .in15(8'hdb), .out(multiplexer_10_out), .sel(in_1[3:0]));
  Multiplexer #(.select(4), .width(8)) multiplexer_11 (
    .in0(8'he0), .in1(8'h32), .in2(8'h3a), .in3(8'ha), .in4(8'h49), .in5(8'h6), .in6(8'h24), .in7(8'h5c),
    .in8(8'hc2), .in9(8'hd3), .in10(8'hac), .in11(8'h62), .in12(8'h91), .in13(8'h95), .in14(8'he4),
    .in15(8'h79), .out(multiplexer_11_out), .sel(in_1[3:0]));
  Multiplexer #(.select(4), .width(8)) multiplexer_12 (
    .in0(8'he7), .in1(8'hc8), .in2(8'h37), .in3(8'h6d), .in4(8'h8d), .in5(8'hd5), .in6(8'h4e), .in7(8'ha9),
    .in8(8'h6c), .in9(8'h56), .in10(8'hf4), .in11(8'hea), .in12(8'h65), .in13(8'h7a), .in14(8'hae),
    .in15(8'h8), .out(multiplexer_12_out), .sel(in_1[3:0]));
  Multiplexer #(.select(4), .width(8)) multiplexer_13 (
    .in0(8'hba), .in1(8'h78), .in2(8'h25), .in3(8'h2e), .in4(8'h1c), .in5(8'ha6), .in6(8'hb4), .in7(8'hc6),
    .in8(8'he8), .in9(8'hdd), .in10(8'h74), .in11(8'h1f), .in12(8'h4b), .in13(8'hbd), .in14(8'h8b),
    .in15(8'h8a), .out(multiplexer_13_out), .sel(in_1[3:0]));
  Multiplexer #(.select(4), .width(8)) multiplexer_14 (
    .in0(8'h70), .in1(8'h3e), .in2(8'hb5), .in3(8'h66), .in4(8'h48), .in5(8'h3), .in6(8'hf6), .in7(8'he),
    .in8(8'h61), .in9(8'h35), .in10(8'h57), .in11(8'hb9), .in12(8'h86), .in13(8'hc1), .in14(8'h1d),
    .in15(8'h9e), .out(multiplexer_14_out), .sel(in_1[3:0]));
  Multiplexer #(.select(4), .width(8)) multiplexer_15 (
    .in0(8'he1), .in1(8'hf8), .in2(8'h98), .in3(8'h11), .in4(8'h69), .in5(8'hd9), .in6(8'h8e), .in7(8'h94),
    .in8(8'h9b), .in9(8'h1e), .in10(8'h87), .in11(8'he9), .in12(8'hce), .in13(8'h55), .in14(8'h28),
    .in15(8'hdf), .out(multiplexer_15_out), .sel(in_1[3:0]));
  Multiplexer #(.select(4), .width(8)) multiplexer_16 (
    .in0(8'h8c), .in1(8'ha1), .in2(8'h89), .in3(8'hd), .in4(8'hbf), .in5(8'he6), .in6(8'h42), .in7(8'h68),
    .in8(8'h41), .in9(8'h99), .in10(8'h2d), .in11(8'hf), .in12(8'hb0), .in13(8'h54), .in14(8'hbb),
    .in15(8'h16), .out(multiplexer_16_out), .sel(in_1[3:0]));
  Multiplexer #(.select(4), .width(8)) multiplexer_17 (
    .in0(multiplexer_1_out), .in1(multiplexer_2_out), .in2(multiplexer_3_out), .in3(multiplexer_4_out),
    .in4(multiplexer_5_out), .in5(multiplexer_6_out), .in6(multiplexer_7_out), .in7(multiplexer_8_out),
    .in8(multiplexer_9_out), .in9(multiplexer_10_out), .in10(multiplexer_11_out), .in11(multiplexer_12_out),
    .in12(multiplexer_13_out), .in13(multiplexer_14_out), .in14(multiplexer_15_out),
    .in15(multiplexer_16_out), .out(out_2), .sel(in_1[7:4]));
endmodule

module ShiftRows (
  input  [63:0] MSBI,
  input  [63:0] LSBI,
  output [63:0] MSBO,
  output [63:0] LSBO
);


  assign LSBO = {LSBI[63:56], LSBI[23:16], MSBI[47:40], MSBI[7:0], LSBI[31:24], MSBI[55:48], MSBI[15:8], LSBI[39:32]};
  assign MSBO = {MSBI[63:56], MSBI[23:16], LSBI[47:40], LSBI[7:0], MSBI[31:24], LSBI[55:48], LSBI[15:8], MSBI[39:32]};
endmodule

module MixColumns (
  input  [63:0] MSBI,
  input  [63:0] LSBI,
  output [63:0] MSBO,
  output [63:0] LSBO
);

  ColumnProcess columnprocess_1 (
    .I_0(MSBI[63:56]), .I_1(MSBI[55:48]), .I_2(MSBI[47:40]), .I_3(MSBI[39:32]), .O_0(MSBO[63:56]),
    .O_1(MSBO[55:48]), .O_2(MSBO[47:40]), .O_3(MSBO[39:32]));
  ColumnProcess columnprocess_2 (
    .I_0(MSBI[31:24]), .I_1(MSBI[23:16]), .I_2(MSBI[15:8]), .I_3(MSBI[7:0]), .O_0(MSBO[31:24]),
    .O_1(MSBO[23:16]), .O_2(MSBO[15:8]), .O_3(MSBO[7:0]));
  ColumnProcess columnprocess_3 (
    .I_0(LSBI[63:56]), .I_1(LSBI[55:48]), .I_2(LSBI[47:40]), .I_3(LSBI[39:32]), .O_0(LSBO[63:56]),
    .O_1(LSBO[55:48]), .O_2(LSBO[47:40]), .O_3(LSBO[39:32]));
  ColumnProcess columnprocess_4 (
    .I_0(LSBI[31:24]), .I_1(LSBI[23:16]), .I_2(LSBI[15:8]), .I_3(LSBI[7:0]), .O_0(LSBO[31:24]),
    .O_1(LSBO[23:16]), .O_2(LSBO[15:8]), .O_3(LSBO[7:0]));
endmodule

module KeyExpansion (
  input  [63:0] MSBI,
  input  [63:0] LSBI,
  input  [3:0] Round,
  output [63:0] MSBO,
  output [63:0] LSBO
);

  wire [7:0] multiplexer_1_out, sbox1_out_2, sbox2_out_2, sbox3_out_2, sbox4_out_2, xor_1_out, xor_2_out,
       xor_3_out, xor_4_out, xor_5_out, xor_6_out, xor_7_out, xor_8_out, xor_9_out, xor_10_out, xor_11_out,
       xor_12_out, xor_13_out, xor_14_out, xor_15_out, xor_16_out, xor_17_out;

  SBox sbox2 (.in_1(LSBI[23:16]), .out_2(sbox2_out_2));
  SBox sbox1 (.in_1(LSBI[31:24]), .out_2(sbox1_out_2));
  SBox sbox3 (.in_1(LSBI[15:8]), .out_2(sbox3_out_2));
  SBox sbox4 (.in_1(LSBI[7:0]), .out_2(sbox4_out_2));
  Multiplexer #(.select(4), .width(8)) multiplexer_1 (
    .in1(8'h1), .in2(8'h2), .in3(8'h4), .in4(8'h8), .in5(8'h10), .in6(8'h20), .in7(8'h40), .in8(8'h80),
    .in9(8'h1b), .in10(8'h36), .out(multiplexer_1_out), .sel(Round));  // open: in0, in11, in12, in13, in14, in15
  assign xor_1_out = sbox2_out_2 ^ multiplexer_1_out;  // XOR_Gate xor_1, 8 bits wide
  assign xor_2_out = MSBI[63:56] ^ xor_1_out;  // XOR_Gate xor_2, 8 bits wide
  assign xor_3_out = MSBI[55:48] ^ sbox3_out_2;  // XOR_Gate xor_3, 8 bits wide
  assign xor_4_out = MSBI[47:40] ^ sbox4_out_2;  // XOR_Gate xor_4, 8 bits wide
  assign xor_5_out = MSBI[39:32] ^ sbox1_out_2;  // XOR_Gate xor_5, 8 bits wide
  assign xor_6_out = MSBI[31:24] ^ xor_2_out;  // XOR_Gate xor_6, 8 bits wide
  assign xor_7_out = MSBI[23:16] ^ xor_3_out;  // XOR_Gate xor_7, 8 bits wide
  assign xor_8_out = MSBI[15:8] ^ xor_4_out;  // XOR_Gate xor_8, 8 bits wide
  assign xor_9_out = MSBI[7:0] ^ xor_5_out;  // XOR_Gate xor_9, 8 bits wide
  assign xor_10_out = xor_6_out ^ LSBI[63:56];  // XOR_Gate xor_10, 8 bits wide
  assign xor_11_out = xor_7_out ^ LSBI[55:48];  // XOR_Gate xor_11, 8 bits wide
  assign xor_12_out = xor_8_out ^ LSBI[47:40];  // XOR_Gate xor_12, 8 bits wide
  assign xor_13_out = xor_9_out ^ LSBI[39:32];  // XOR_Gate xor_13, 8 bits wide
  assign xor_14_out = xor_10_out ^ LSBI[31:24];  // XOR_Gate xor_14, 8 bits wide
  assign xor_15_out = xor_11_out ^ LSBI[23:16];  // XOR_Gate xor_15, 8 bits wide
  assign xor_16_out = xor_12_out ^ LSBI[15:8];  // XOR_Gate xor_16, 8 bits wide
  assign xor_17_out = xor_13_out ^ LSBI[7:0];  // XOR_Gate xor_17, 8 bits wide
  Multiplexer #(.select(4), .width(64)) multiplexer_2 (
    .in0(LSBI),
    .in1({xor_10_out, xor_11_out, xor_12_out, xor_13_out, xor_14_out, xor_15_out, xor_16_out, xor_17_out}),
    .in2({xor_10_out, xor_11_out, xor_12_out, xor_13_out, xor_14_out, xor_15_out, xor_16_out, xor_17_out}),
    .in3({xor_10_out, xor_11_out, xor_12_out, xor_13_out, xor_14_out, xor_15_out, xor_16_out, xor_17_out}),
    .in4({xor_10_out, xor_11_out, xor_12_out, xor_13_out, xor_14_out, xor_15_out, xor_16_out, xor_17_out}),
    .in5({xor_10_out, xor_11_out, xor_12_out, xor_13_out, xor_14_out, xor_15_out, xor_16_out, xor_17_out}),
    .in6({xor_10_out, xor_11_out, xor_12_out, xor_13_out, xor_14_out, xor_15_out, xor_16_out, xor_17_out}),
    .in7({xor_10_out, xor_11_out, xor_12_out, xor_13_out, xor_14_out, xor_15_out, xor_16_out, xor_17_out}),
    .in8({xor_10_out, xor_11_out, xor_12_out, xor_13_out, xor_14_out, xor_15_out, xor_16_out, xor_17_out}),
    .in9({xor_10_out, xor_11_out, xor_12_out, xor_13_out, xor_14_out, xor_15_out, xor_16_out, xor_17_out}),
    .in10({xor_10_out, xor_11_out, xor_12_out, xor_13_out, xor_14_out, xor_15_out, xor_16_out, xor_17_out}),
    .out(LSBO), .sel(Round));  // open: in11, in12, in13, in14, in15
  Multiplexer #(.select(4), .width(64)) multiplexer_3 (
    .in0(MSBI),
    .in1({xor_2_out, xor_3_out, xor_4_out, xor_5_out, xor_6_out, xor_7_out, xor_8_out, xor_9_out}),
    .in2({xor_2_out, xor_3_out, xor_4_out, xor_5_out, xor_6_out, xor_7_out, xor_8_out, xor_9_out}),
    .in3({xor_2_out, xor_3_out, xor_4_out, xor_5_out, xor_6_out, xor_7_out, xor_8_out, xor_9_out}),
    .in4({xor_2_out, xor_3_out, xor_4_out, xor_5_out, xor_6_out, xor_7_out, xor_8_out, xor_9_out}),
    .in5({xor_2_out, xor_3_out, xor_4_out, xor_5_out, xor_6_out, xor_7_out, xor_8_out, xor_9_out}),
    .in6({xor_2_out, xor_3_out, xor_4_out, xor_5_out, xor_6_out, xor_7_out, xor_8_out, xor_9_out}),
    .in7({xor_2_out, xor_3_out, xor_4_out, xor_5_out, xor_6_out, xor_7_out, xor_8_out, xor_9_out}),
    .in8({xor_2_out, xor_3_out, xor_4_out, xor_5_out, xor_6_out, xor_7_out, xor_8_out, xor_9_out}),
    .in9({xor_2_out, xor_3_out, xor_4_out, xor_5_out, xor_6_out, xor_7_out, xor_8_out, xor_9_out}),
    .in10({xor_2_out, xor_3_out, xor_4_out, xor_5_out, xor_6_out, xor_7_out, xor_8_out, xor_9_out}),
    .out(MSBO), .sel(Round));  // open: in11, in12, in13, in14, in15
endmodule

module AddRoundKey (
  input  [63:0] MSBI,
  input  [63:0] KMSBI,
  input  [63:0] LSBI,
  input  [63:0] KLSBI,
  output [63:0] MSBO,
  output [63:0] LSBO
);

  assign MSBO = MSBI ^ KMSBI;  // XOR_Gate xor_1, 64 bits wide
  assign LSBO = LSBI ^ KLSBI;  // XOR_Gate xor_2, 64 bits wide
endmodule

module Multiplication (
  input  [7:0] in_data,
  input  [1:0] sel,
  output [7:0] out_data
);

  wire [7:0] multiplexer_1_out, xor_1_out, xor_2_out;

  assign xor_1_out = {in_data[6:0], 1'b0} ^ 8'h1b;  // XOR_Gate xor_1, 8 bits wide
  Multiplexer #(.width(8)) multiplexer_1 (
    .in0({in_data[6:0], 1'b0}), .in1(xor_1_out), .out(multiplexer_1_out), .sel(in_data[7]));
  assign xor_2_out = multiplexer_1_out ^ in_data;  // XOR_Gate xor_2, 8 bits wide
  Multiplexer #(.select(2), .width(8)) multiplexer_2 (
    .in1(in_data), .in2(multiplexer_1_out), .in3(xor_2_out), .out(out_data), .sel(sel));  // open: in0
endmodule

module CellProcess (
  input  [7:0] in_data_0,
  input  [7:0] in_data_1,
  input  [7:0] in_data_2,
  input  [7:0] in_data_3,
  input  [1:0] row,
  output [7:0] out_6
);

  wire [1:0] multiplexer_1_out, multiplexer_2_out, multiplexer_3_out, multiplexer_4_out;
  wire [7:0] multiplication_1_out_data, multiplication_2_out_data, multiplication_3_out_data,
       multiplication_4_out_data, xor_1_out, xor_3_out;

  Multiplexer #(.select(2), .width(2)) multiplexer_1 (
    .in0(2'b10), .in1(2'b01), .in2(2'b01), .in3(2'b11), .out(multiplexer_1_out), .sel(row));
  Multiplexer #(.select(2), .width(2)) multiplexer_2 (
    .in0(2'b11), .in1(2'b10), .in2(2'b01), .in3(2'b01), .out(multiplexer_2_out), .sel(row));
  Multiplexer #(.select(2), .width(2)) multiplexer_3 (
    .in0(2'b01), .in1(2'b11), .in2(2'b10), .in3(2'b01), .out(multiplexer_3_out), .sel(row));
  Multiplexer #(.select(2), .width(2)) multiplexer_4 (
    .in0(2'b01), .in1(2'b01), .in2(2'b11), .in3(2'b10), .out(multiplexer_4_out), .sel(row));
  Multiplication multiplication_1 (.in_data(in_data_0), .sel(multiplexer_1_out), .out_data(multiplication_1_out_data));
  Multiplication multiplication_2 (.in_data(in_data_1), .sel(multiplexer_2_out), .out_data(multiplication_2_out_data));
  Multiplication multiplication_3 (.in_data(in_data_2), .sel(multiplexer_3_out), .out_data(multiplication_3_out_data));
  Multiplication multiplication_4 (.in_data(in_data_3), .sel(multiplexer_4_out), .out_data(multiplication_4_out_data));
  assign xor_1_out = multiplication_1_out_data ^ multiplication_2_out_data;  // XOR_Gate xor_1, 8 bits wide
  assign out_6 = xor_1_out ^ xor_3_out;  // XOR_Gate xor_2, 8 bits wide
  assign xor_3_out = multiplication_3_out_data ^ multiplication_4_out_data;  // XOR_Gate xor_3, 8 bits wide
endmodule

module ColumnProcess (
  input  [7:0] I_0,
  input  [7:0] I_1,
  input  [7:0] I_2,
  input  [7:0] I_3,
  output [7:0] O_0,
  output [7:0] O_1,
  output [7:0] O_2,
  output [7:0] O_3
);

  CellProcess cellprocess_1 (
    .row(2'b00), .in_data_0(I_0), .in_data_1(I_1), .in_data_2(I_2), .in_data_3(I_3), .out_6(O_0));
  CellProcess cellprocess_2 (
    .row(2'b01), .in_data_0(I_0), .in_data_1(I_1), .in_data_2(I_2), .in_data_3(I_3), .out_6(O_1));
  CellProcess cellprocess_3 (
    .row(2'b10), .in_data_0(I_0), .in_data_1(I_1), .in_data_2(I_2), .in_data_3(I_3), .out_6(O_2));
  CellProcess cellprocess_4 (
    .row(2'b11), .in_data_0(I_0), .in_data_1(I_1), .in_data_2(I_2), .in_data_3(I_3), .out_6(O_3));
endmodule

module Round (
  input  [63:0] MSBData,
  input  [63:0] LSBData,
  input  [63:0] MSBKey,
  input  [63:0] LSBKey,
  input  [3:0] RoundNum,
  input  Rst,
  output [63:0] MSBDataOut,
  output [63:0] LSBDataOut,
  output [63:0] MSBKeyOut,
  output [63:0] LSBKeyOut
);

  wire [63:0] addroundkey_1_lsbo, addroundkey_1_msbo, keyexpansion_1_lsbo, keyexpansion_1_msbo,
       mixcolumns_1_lsbo, mixcolumns_1_msbo, multiplexer_1_out, multiplexer_2_out, shiftrows_1_lsbo,
       shiftrows_1_msbo, subbytes_1_lsbo, subbytes_1_msbo;

  SubBytes subbytes_1 (.MSBI(MSBData), .LSBI(LSBData), .MSBO(subbytes_1_msbo), .LSBO(subbytes_1_lsbo));
  KeyExpansion keyexpansion_1 (
    .Round(RoundNum), .MSBI(MSBKey), .LSBI(LSBKey), .MSBO(keyexpansion_1_msbo), .LSBO(keyexpansion_1_lsbo));
  ShiftRows shiftrows_1 (
    .MSBI(subbytes_1_msbo), .LSBI(subbytes_1_lsbo), .MSBO(shiftrows_1_msbo), .LSBO(shiftrows_1_lsbo));
  Multiplexer #(.select(4), .width(64)) multiplexer_1 (
    .in0(MSBData), .in1(mixcolumns_1_msbo), .in2(mixcolumns_1_msbo), .in3(mixcolumns_1_msbo),
    .in4(mixcolumns_1_msbo), .in5(mixcolumns_1_msbo), .in6(mixcolumns_1_msbo), .in7(mixcolumns_1_msbo),
    .in8(mixcolumns_1_msbo), .in9(mixcolumns_1_msbo), .in10(shiftrows_1_msbo), .out(multiplexer_1_out),
    .sel(RoundNum));  // open: in11, in12, in13, in14, in15
  MixColumns mixcolumns_1 (
    .MSBI(shiftrows_1_msbo), .LSBI(shiftrows_1_lsbo), .MSBO(mixcolumns_1_msbo), .LSBO(mixcolumns_1_lsbo));
  Multiplexer #(.select(4), .width(64)) multiplexer_2 (
    .in0(LSBData), .in1(mixcolumns_1_lsbo), .in2(mixcolumns_1_lsbo), .in3(mixcolumns_1_lsbo),
    .in4(mixcolumns_1_lsbo), .in5(mixcolumns_1_lsbo), .in6(mixcolumns_1_lsbo), .in7(mixcolumns_1_lsbo),
    .in8(mixcolumns_1_lsbo), .in9(mixcolumns_1_lsbo), .in10(shiftrows_1_lsbo), .out(multiplexer_2_out),
    .sel(RoundNum));  // open: in11, in12, in13, in14, in15
  AddRoundKey addroundkey_1 (
    .MSBI(multiplexer_1_out), .KMSBI(keyexpansion_1_msbo), .LSBI(multiplexer_2_out),
    .KLSBI(keyexpansion_1_lsbo), .MSBO(addroundkey_1_msbo), .LSBO(addroundkey_1_lsbo));
  Multiplexer #(.width(64)) multiplexer_3 (.in0({64{1'b0}}), .in1(addroundkey_1_msbo), .out(MSBDataOut), .sel(Rst));
  Multiplexer #(.width(64)) multiplexer_4 (.in0({64{1'b0}}), .in1(addroundkey_1_lsbo), .out(LSBDataOut), .sel(Rst));
  Multiplexer #(.width(64)) multiplexer_5 (.in0({64{1'b0}}), .in1(keyexpansion_1_msbo), .out(MSBKeyOut), .sel(Rst));
  Multiplexer #(.width(64)) multiplexer_6 (.in0({64{1'b0}}), .in1(keyexpansion_1_lsbo), .out(LSBKeyOut), .sel(Rst));
endmodule

module Top (
  input  [63:0] Plain0,
  input  [63:0] Plain1,
  input  [63:0] Key0,
  input  [63:0] Key1,
  input  Rst,
  output [63:0] Cipher0,
  output [63:0] Cipher1
);

  wire Clk_out;
  wire [63:0] register_1_q, register_2_q, register_3_q, register_4_q, register_5_q, register_6_q,
       register_7_q, register_8_q, register_9_q, register_10_q, register_11_q, register_12_q, register_13_q,
       register_14_q, register_15_q, register_16_q, register_17_q, register_18_q, register_19_q,
       register_20_q, register_21_q, register_22_q, register_23_q, register_24_q, register_25_q,
       register_26_q, register_27_q, register_28_q, register_29_q, register_30_q, register_31_q,
       register_32_q, register_33_q, register_34_q, register_35_q, register_36_q, register_37_q,
       register_38_q, register_39_q, register_40_q, Round0_lsbdataout, Round0_lsbkeyout, Round0_msbdataout,
       Round0_msbkeyout, Round1_lsbdataout, Round1_lsbkeyout, Round1_msbdataout, Round1_msbkeyout,
       Round2_lsbdataout, Round2_lsbkeyout, Round2_msbdataout, Round2_msbkeyout, Round3_lsbdataout,
       Round3_lsbkeyout, Round3_msbdataout, Round3_msbkeyout, Round4_lsbdataout, Round4_lsbkeyout,
       Round4_msbdataout, Round4_msbkeyout, Round5_lsbdataout, Round5_lsbkeyout, Round5_msbdataout,
       Round5_msbkeyout, Round6_lsbdataout, Round6_lsbkeyout, Round6_msbdataout, Round6_msbkeyout,
       Round7_lsbdataout, Round7_lsbkeyout, Round7_msbdataout, Round7_msbkeyout, Round8_lsbdataout,
       Round8_lsbkeyout, Round8_msbdataout, Round8_msbkeyout, Round9_lsbdataout, Round9_lsbkeyout,
       Round9_msbdataout, Round9_msbkeyout;

  Clock Clk (.out(Clk_out));
  Register #(.width(64)) register_1 (.D(Round5_msbdataout), .clk(Clk_out), .Q(register_1_q));  // open: en, clr
  Round Round5 (
    .Rst(Rst), .RoundNum(4'b0101), .MSBData(register_37_q), .LSBData(register_38_q), .MSBKey(register_39_q),
    .LSBKey(register_40_q), .MSBDataOut(Round5_msbdataout), .LSBDataOut(Round5_lsbdataout),
    .MSBKeyOut(Round5_msbkeyout), .LSBKeyOut(Round5_lsbkeyout));
  Register #(.width(64)) register_2 (.D(Round5_lsbdataout), .clk(Clk_out), .Q(register_2_q));  // open: en, clr
  Register #(.width(64)) register_3 (.D(Round5_msbkeyout), .clk(Clk_out), .Q(register_3_q));  // open: en, clr
  Register #(.width(64)) register_4 (.D(Round5_lsbkeyout), .clk(Clk_out), .Q(register_4_q));  // open: en, clr
  Round Round0 (
    .Rst(Rst), .RoundNum(4'b0000), .MSBData(Plain0), .LSBData(Plain1), .MSBKey(Key0), .LSBKey(Key1),
    .MSBDataOut(Round0_msbdataout), .LSBDataOut(Round0_lsbdataout), .MSBKeyOut(Round0_msbkeyout),
    .LSBKeyOut(Round0_lsbkeyout));
  Register #(.width(64)) register_5 (.D(Round0_msbdataout), .clk(Clk_out), .Q(register_5_q));  // open: en, clr
  Register #(.width(64)) register_6 (.D(Round0_lsbdataout), .clk(Clk_out), .Q(register_6_q));  // open: en, clr
  Register #(.width(64)) register_7 (.D(Round0_msbkeyout), .clk(Clk_out), .Q(register_7_q));  // open: en, clr
  Register #(.width(64)) register_8 (.D(Round0_lsbkeyout), .clk(Clk_out), .Q(register_8_q));  // open: en, clr
  Round Round6 (
    .Rst(Rst), .RoundNum(4'b0110), .MSBData(register_1_q), .LSBData(register_2_q), .MSBKey(register_3_q),
    .LSBKey(register_4_q), .MSBDataOut(Round6_msbdataout), .LSBDataOut(Round6_lsbdataout),
    .MSBKeyOut(Round6_msbkeyout), .LSBKeyOut(Round6_lsbkeyout));
  Register #(.width(64)) register_9 (.D(Round6_msbdataout), .clk(Clk_out), .Q(register_9_q));  // open: en, clr
  Register #(.width(64)) register_10 (.D(Round6_lsbdataout), .clk(Clk_out), .Q(register_10_q));  // open: en, clr
  Register #(.width(64)) register_11 (.D(Round6_msbkeyout), .clk(Clk_out), .Q(register_11_q));  // open: en, clr
  Register #(.width(64)) register_12 (.D(Round6_lsbkeyout), .clk(Clk_out), .Q(register_12_q));  // open: en, clr
  Round Round1 (
    .Rst(Rst), .RoundNum(4'b0001), .MSBData(register_5_q), .LSBData(register_6_q), .MSBKey(register_7_q),
    .LSBKey(register_8_q), .MSBDataOut(Round1_msbdataout), .LSBDataOut(Round1_lsbdataout),
    .MSBKeyOut(Round1_msbkeyout), .LSBKeyOut(Round1_lsbkeyout));
  Register #(.width(64)) register_13 (.D(Round1_msbdataout), .clk(Clk_out), .Q(register_13_q));  // open: en, clr
  Register #(.width(64)) register_14 (.D(Round1_lsbdataout), .clk(Clk_out), .Q(register_14_q));  // open: en, clr
  Register #(.width(64)) register_15 (.D(Round1_msbkeyout), .clk(Clk_out), .Q(register_15_q));  // open: en, clr
  Register #(.width(64)) register_16 (.D(Round1_lsbkeyout), .clk(Clk_out), .Q(register_16_q));  // open: en, clr
  Round Round7 (
    .Rst(Rst), .RoundNum(4'b0111), .MSBData(register_9_q), .LSBData(register_10_q), .MSBKey(register_11_q),
    .LSBKey(register_12_q), .MSBDataOut(Round7_msbdataout), .LSBDataOut(Round7_lsbdataout),
    .MSBKeyOut(Round7_msbkeyout), .LSBKeyOut(Round7_lsbkeyout));
  Register #(.width(64)) register_17 (.D(Round7_msbdataout), .clk(Clk_out), .Q(register_17_q));  // open: en, clr
  Register #(.width(64)) register_18 (.D(Round7_lsbdataout), .clk(Clk_out), .Q(register_18_q));  // open: en, clr
  Register #(.width(64)) register_19 (.D(Round7_msbkeyout), .clk(Clk_out), .Q(register_19_q));  // open: en, clr
  Register #(.width(64)) register_20 (.D(Round7_lsbkeyout), .clk(Clk_out), .Q(register_20_q));  // open: en, clr
  Round Round2 (
    .Rst(Rst), .RoundNum(4'b0010), .MSBData(register_13_q), .LSBData(register_14_q), .MSBKey(register_15_q),
    .LSBKey(register_16_q), .MSBDataOut(Round2_msbdataout), .LSBDataOut(Round2_lsbdataout),
    .MSBKeyOut(Round2_msbkeyout), .LSBKeyOut(Round2_lsbkeyout));
  Register #(.width(64)) register_21 (.D(Round2_msbdataout), .clk(Clk_out), .Q(register_21_q));  // open: en, clr
  Register #(.width(64)) register_22 (.D(Round2_lsbdataout), .clk(Clk_out), .Q(register_22_q));  // open: en, clr
  Register #(.width(64)) register_23 (.D(Round2_msbkeyout), .clk(Clk_out), .Q(register_23_q));  // open: en, clr
  Register #(.width(64)) register_24 (.D(Round2_lsbkeyout), .clk(Clk_out), .Q(register_24_q));  // open: en, clr
  Round Round8 (
    .Rst(Rst), .RoundNum(4'b1000), .MSBData(register_17_q), .LSBData(register_18_q), .MSBKey(register_19_q),
    .LSBKey(register_20_q), .MSBDataOut(Round8_msbdataout), .LSBDataOut(Round8_lsbdataout),
    .MSBKeyOut(Round8_msbkeyout), .LSBKeyOut(Round8_lsbkeyout));
  Register #(.width(64)) register_25 (.D(Round8_msbdataout), .clk(Clk_out), .Q(register_25_q));  // open: en, clr
  Register #(.width(64)) register_26 (.D(Round8_lsbdataout), .clk(Clk_out), .Q(register_26_q));  // open: en, clr
  Register #(.width(64)) register_27 (.D(Round8_msbkeyout), .clk(Clk_out), .Q(register_27_q));  // open: en, clr
  Register #(.width(64)) register_28 (.D(Round8_lsbkeyout), .clk(Clk_out), .Q(register_28_q));  // open: en, clr
  Round Round3 (
    .Rst(Rst), .RoundNum(4'b0011), .MSBData(register_21_q), .LSBData(register_22_q), .MSBKey(register_23_q),
    .LSBKey(register_24_q), .MSBDataOut(Round3_msbdataout), .LSBDataOut(Round3_lsbdataout),
    .MSBKeyOut(Round3_msbkeyout), .LSBKeyOut(Round3_lsbkeyout));
  Register #(.width(64)) register_29 (.D(Round3_msbdataout), .clk(Clk_out), .Q(register_29_q));  // open: en, clr
  Register #(.width(64)) register_30 (.D(Round3_lsbdataout), .clk(Clk_out), .Q(register_30_q));  // open: en, clr
  Register #(.width(64)) register_31 (.D(Round3_msbkeyout), .clk(Clk_out), .Q(register_31_q));  // open: en, clr
  Register #(.width(64)) register_32 (.D(Round3_lsbkeyout), .clk(Clk_out), .Q(register_32_q));  // open: en, clr
  Round Round9 (
    .Rst(Rst), .RoundNum(4'b1001), .MSBData(register_25_q), .LSBData(register_26_q), .MSBKey(register_27_q),
    .LSBKey(register_28_q), .MSBDataOut(Round9_msbdataout), .LSBDataOut(Round9_lsbdataout),
    .MSBKeyOut(Round9_msbkeyout), .LSBKeyOut(Round9_lsbkeyout));
  Register #(.width(64)) register_33 (.D(Round9_msbdataout), .clk(Clk_out), .Q(register_33_q));  // open: en, clr
  Register #(.width(64)) register_34 (.D(Round9_lsbdataout), .clk(Clk_out), .Q(register_34_q));  // open: en, clr
  Register #(.width(64)) register_35 (.D(Round9_msbkeyout), .clk(Clk_out), .Q(register_35_q));  // open: en, clr
  Register #(.width(64)) register_36 (.D(Round9_lsbkeyout), .clk(Clk_out), .Q(register_36_q));  // open: en, clr
  Register #(.width(64)) register_37 (.D(Round4_msbdataout), .clk(Clk_out), .Q(register_37_q));  // open: en, clr
  Round Round4 (
    .Rst(Rst), .RoundNum(4'b0100), .MSBData(register_29_q), .LSBData(register_30_q), .MSBKey(register_31_q),
    .LSBKey(register_32_q), .MSBDataOut(Round4_msbdataout), .LSBDataOut(Round4_lsbdataout),
    .MSBKeyOut(Round4_msbkeyout), .LSBKeyOut(Round4_lsbkeyout));
  Register #(.width(64)) register_38 (.D(Round4_lsbdataout), .clk(Clk_out), .Q(register_38_q));  // open: en, clr
  Register #(.width(64)) register_39 (.D(Round4_msbkeyout), .clk(Clk_out), .Q(register_39_q));  // open: en, clr
  Register #(.width(64)) register_40 (.D(Round4_lsbkeyout), .clk(Clk_out), .Q(register_40_q));  // open: en, clr
  Round round_1 (
    .Rst(Rst), .RoundNum(4'b1010), .MSBData(register_33_q), .LSBData(register_34_q), .MSBKey(register_35_q),
    .LSBKey(register_36_q), .MSBDataOut(Cipher0), .LSBDataOut(Cipher1));  // open: MSBKeyOut, LSBKeyOut

  // Notes on the sheet:
  //   Rst: initial=0x1
  //   Plain0: initial=0xa88a459d49a45d64
  //   Plain1: initial=0x262d4cb5098ecdbb
  //   Key0: initial=0xb4ef5bcb3e92e211
  //   Key1: initial=0x23e951cf6f8f188e
endmodule
